// Logisim project projetoic.circ as structural Verilog: 9 circuits, main circuit somadorCompleto
module somadorCompleto (
  input  A,
  input  B,
  input  C,
  output Soma,
  output Carry_Out
);

  wire and_1_out, and_2_out, and_3_out, and_4_out, not_1_out, not_2_out, not_3_out, xor_1_out;

  not not_1 (not_1_out, A);
  not not_2 (not_2_out, B);
  not not_3 (not_3_out, C);
  xor xor_1 (xor_1_out, A, B);
  and and_1 (and_1_out, not_1_out, B, C);
  and and_2 (and_2_out, A, not_2_out, C);
  and and_3 (and_3_out, A, B, not_3_out);
  and and_4 (and_4_out, A, B, C);
  xor xor_2 (Soma, xor_1_out, C);
  or or_1 (Carry_Out, and_1_out, and_2_out, and_3_out, and_4_out);

  // Notes on the sheet:
  //   Somador Completo
endmodule

module main (
  input  A,
  input  A_2,
  input  B,
  input  B_2,
  input  C1,
  input  C0,
  input  A1,
  input  B1,
  input  A0,
  input  B0,
  input  C1_2,
  input  C0_2,
  input  A0_2,
  input  A1_2,
  input  B0_2,
  input  B1_2,
  input  [1:0] A_3,
  input  [1:0] B_3,
  output out_19,
  output out_20,
  output C,
  output Erro
);

  wire divisor_2_1_bit_0, divisor_2_1_bit_1, multiplex_1_saida, multiplex_2_saida,
       multiplicadorcompleto_1_y0, multiplicadorcompleto_1_y1, somadorcompleto_1_carry_out,
       somadorcompleto_1_soma, somadorcompleto_2_soma, subtrator_full_1_out_4, subtrator_full_1_out_5,
       subtrator_full_2_out_4;

  somadorCompleto somadorcompleto_1 (
    .A(A), .B(B), .C(1'b0), .Soma(somadorcompleto_1_soma), .Carry_Out(somadorcompleto_1_carry_out));
  subtrator_full subtrator_full_1 (
    .in_1(A1), .in_2(B1), .in_3(1'b0), .out_4(subtrator_full_1_out_4), .out_5(subtrator_full_1_out_5));
  multiplicadorCompleto multiplicadorcompleto_1 (
    .A0(A0_2), .A1(A1_2), .B0(B0_2), .B1(B1_2), .C(C), .Y0(multiplicadorcompleto_1_y0),
    .Y1(multiplicadorcompleto_1_y1));
  divisor_2 divisor_2_1 (.in_1(A_3), .in_2(B_3), .erro(Erro), .bit_1(divisor_2_1_bit_1), .bit_0(divisor_2_1_bit_0));
  subtrator_full subtrator_full_2 (
    .in_1(A0), .in_2(B0), .in_3(subtrator_full_1_out_5), .out_4(subtrator_full_2_out_4), .out_5(out_20));
  somadorCompleto somadorcompleto_2 (
    .A(A_2), .B(B_2), .C(somadorcompleto_1_carry_out), .Soma(somadorcompleto_2_soma), .Carry_Out(out_19));
  multiplex multiplex_1 (
    .E0(somadorcompleto_1_soma), .E1(subtrator_full_1_out_4), .E2(multiplicadorcompleto_1_y1),
    .E3(divisor_2_1_bit_1), .C1(C1), .C0(C0), .Saida(multiplex_1_saida));
  multiplex multiplex_2 (
    .E0(somadorcompleto_2_soma), .E1(subtrator_full_2_out_4), .E2(multiplicadorcompleto_1_y0),
    .E3(divisor_2_1_bit_0), .C1(C1_2), .C0(C0_2), .Saida(multiplex_2_saida));
  LED _0 (.in(multiplex_1_saida));
  LED _1 (.in(multiplex_2_saida));

  // Notes on the sheet:
  //   Somador Completo
  //   Subtrator Completo
  //   Multiplicador Completo
  //   Divisor
  //   00 = Somador
  //   01 = Subtrator
  //   10 = Multiplicador
  //   11 = Divisor
endmodule

module multiplex (
  input  E0,
  input  E1,
  input  E2,
  input  E3,
  input  C1,
  input  C0,
  output Saida
);

  wire and_1_out, and_2_out, and_3_out, and_4_out, not_1_out, not_2_out, not_3_out, not_4_out;

  not not_1 (not_1_out, C0);
  not not_2 (not_2_out, C1);
  not not_3 (not_3_out, C1);
  not not_4 (not_4_out, C0);
  and and_1 (and_1_out, E0, not_1_out, not_2_out);
  and and_2 (and_2_out, E1, C0, not_3_out);
  and and_3 (and_3_out, E2, not_4_out, C1);
  and and_4 (and_4_out, E3, C0, C1);
  or or_1 (Saida, and_1_out, and_2_out, and_3_out, and_4_out);
endmodule

module meioMultiplicador (
  input  A0,
  input  A1,
  input  B0,
  input  B1,
  output Y0,
  output P1,
  output P2
);

  and and_1 (Y0, A0, B0);
  and and_2 (P1, A1, B0);
  and and_3 (P2, A0, B1);
endmodule

module meioSomador (
  input  A,
  input  B,
  output S,
  output C
);

  xor xor_1 (S, A, B);
  and and_1 (C, A, B);
endmodule

module multiplicadorCompleto (
  input  A0,
  input  A1,
  input  B0,
  input  B1,
  output Y0,
  output Y1,
  output C
);

  wire meiomultiplicador_1_p1, meiomultiplicador_1_p2;

  meioMultiplicador meiomultiplicador_1 (
    .A0(A0), .A1(A1), .B0(B0), .B1(B1), .Y0(Y0), .P1(meiomultiplicador_1_p1), .P2(meiomultiplicador_1_p2));
  meioSomador meiosomador_1 (.A(meiomultiplicador_1_p1), .B(meiomultiplicador_1_p2), .S(Y1), .C(C));
endmodule

module subtrator_meio (
  input  in_1,
  input  in_2,
  output out_3,
  output out_4
);

  wire not_1_out;

  not not_1 (not_1_out, in_1);
  or or_1 (out_3, in_1, in_2);
  and and_1 (out_4, not_1_out, in_2);
endmodule

module subtrator_full (
  input  in_1,
  input  in_2,
  input  in_3,
  output out_4,
  output out_5
);

  wire and_1_out, and_2_out, and_3_out, not_1_out, xor_1_out;

  not not_1 (not_1_out, in_1);
  xor xor_1 (xor_1_out, in_1, in_2);
  and and_1 (and_1_out, not_1_out, in_2);
  and and_2 (and_2_out, not_1_out, in_3);
  and and_3 (and_3_out, in_2, in_3);
  xor xor_2 (out_4, xor_1_out, in_3);
  or or_1 (out_5, and_1_out, and_2_out, and_3_out);
endmodule

module divisor_2 (
  input  [1:0] in_1,
  input  [1:0] in_2,
  output erro,
  output bit_1,
  output bit_0
);

  wire and_3_out, and_4_out, not_1_out, not_2_out, not_3_out, not_4_out, not_5_out;

  not not_1 (not_1_out, in_2[0]);
  not not_2 (not_2_out, in_2[1]);
  not not_3 (not_3_out, in_2[1]);
  not not_4 (not_4_out, in_2[1]);
  not not_5 (not_5_out, in_2[0]);
  and and_1 (erro, not_1_out, not_2_out);
  and and_2 (bit_1, in_1[1], not_3_out, in_2[0]);
  and and_3 (and_3_out, in_1[0], not_4_out, in_2[0]);
  and and_4 (and_4_out, in_1[1], in_2[1], not_5_out);
  or or_1 (bit_0, and_3_out, and_4_out);
endmodule
